// Digital circuit a-cpu-2.dig as structural Verilog
module a_cpu_2 (
  input  clk
);

  wire C0, C1, C2, CLK_t, CLK_T_t, END_OF_COPY, INC_R, LD_MEM, LD_T, nCLK, nCLK_RAM, nCOPY, nLD_C, nLD_GPO,
       nLD_I, nLD_RH, nLD_RL, nLD_S, nLD_TF, nM_C, nOE_ALU, nOE_GPI, nOE_MEM, nOE_T, nR, RH0_ovf, RL0_ovf,
       RL1_ovf, SEL_C0, SEL_C1, SEL_C2, SEL_nM_CN, TF_0, TF_1, TF_2;
  wire [3:0] dipswitch_1_out, GPI_q, GPO_q, R_0__3, R_8__11, S;
  wire [7:0] ALU_d, BUS, I, RAM_q, T_q;
  wire [7:4] R_8__15;
  wire [7:5] R_0__7;
  wire [15:0] ADDRESS;

  nand nand_1 (nCLK, clk, 1'b1);
  nand nand_2 (CLK_t, nCLK, 1'b1);
  nand nand_3 (nCLK_RAM, nCLK, LD_MEM);
  nand nand_4 (CLK_T_t, nCLK, LD_T);
  Reset reset_1 (.out(nR));
  // Probe ~CLK on nCLK
  // Probe CLK on CLK_t
  // Probe RAM ~WE on nCLK_RAM
  // Probe T CLK on CLK_T_t
  // Probe on {SEL_nM_CN, SEL_C2, SEL_C1, SEL_C0}
  DipSwitch dipswitch_1 (.out(dipswitch_1_out[0]));
  DipSwitch dipswitch_2 (.out(dipswitch_1_out[1]));
  DipSwitch dipswitch_3 (.out(dipswitch_1_out[2]));
  DipSwitch dipswitch_4 (.out(dipswitch_1_out[3]));
  CounterPreset #(.Bits(4)) u_S (
    .en(1'b1), .C(CLK_t), .dir(1'b0), .in(4'b0000), .ld(~nLD_S), .clr(~nR), .out(S));  // open: ovf
  Register #(.Bits(8)) u_I (.D(BUS), .C(CLK_t), .en(~nLD_I), .Q(I));
  Register #(.Bits(8)) T (.D(BUS), .C(CLK_T_t), .en(1'b1), .Q(T_q));
  CounterPreset #(.Bits(4)) C (
    .en(1'b0), .C(CLK_t), .dir(1'b0), .in({SEL_nM_CN, SEL_C2, SEL_C1, SEL_C0}), .ld(~nLD_C), .clr(~nR),
    .out({nM_C, C2, C1, C0}));  // open: ovf
  Register #(.Bits(4)) GPO (.D({SEL_nM_CN, SEL_C2, SEL_C1, SEL_C0}), .C(CLK_t), .en(~nLD_GPO), .Q(GPO_q));
  Register #(.Bits(4)) GPI (.D(dipswitch_1_out), .C(CLK_T_t), .en(1'b1), .Q(GPI_q));
  // Probe S on S
  // Probe on I
  assign BUS = ~nOE_T ? T_q : 8'bz;  // DriverInvSel driverinvsel_1
  // Probe on T_q
  // Probe on {nM_C, C2, C1, C0}
  LED led_1 (.in(GPO_q[0]));
  LED led_2 (.in(GPO_q[1]));
  LED led_3 (.in(GPO_q[2]));
  LED led_4 (.in(GPO_q[3]));
  assign BUS = ~nOE_GPI ? {4'b0000, GPI_q} : 8'bz;  // DriverInvSel driverinvsel_2
  // Probe on {4'b0000, GPI_q}
  CounterPreset #(.Bits(4)) RL0 (
    .en(INC_R), .C(CLK_t), .dir(1'b0), .in(BUS[3:0]), .ld(~nLD_RL), .clr(~nR), .out(R_0__3), .ovf(RL0_ovf));
  CounterPreset #(.Bits(4)) RL1 (
    .en(RL0_ovf), .C(CLK_t), .dir(1'b0), .in(BUS[7:4]), .ld(~nLD_RL), .clr(~nR), .out({R_0__7, END_OF_COPY}),
    .ovf(RL1_ovf));
  CounterPreset #(.Bits(4)) RH0 (
    .en(RL1_ovf), .C(CLK_t), .dir(1'b0), .in(BUS[3:0]), .ld(~nLD_RH), .clr(~nR), .out(R_8__11), .ovf(RH0_ovf));
  CounterPreset #(.Bits(4)) RH1 (
    .en(RH0_ovf), .C(CLK_t), .dir(1'b0), .in(BUS[7:4]), .ld(~nLD_RH), .clr(~nR), .out(R_8__15));  // open: ovf
  // Probe on BUS
  // Probe on {R_0__7, END_OF_COPY, R_0__3}
  // Probe on {R_8__15, R_8__11}
  Multiplexer #(.Bits(4)) multiplexer_1 (.sel(nM_C), .in_0(R_0__3), .in_1({1'b0, C2, C1, C0}), .out(ADDRESS[3:0]));
  assign ADDRESS[7:4] = {R_0__7, END_OF_COPY} | {4{nM_C}};  // Or or_1, 4 bits wide
  assign ADDRESS[11:8] = R_8__11 | {4{nM_C}};  // Or or_2, 4 bits wide
  assign ADDRESS[15:12] = R_8__15 | {4{nM_C}};  // Or or_3, 4 bits wide
  RAMAsync #(.AddrBits(16), .Bits(8)) RAM (.A(ADDRESS), .D(BUS), .we(~nCLK_RAM), .Q(RAM_q));
  CounterPreset #(.Bits(4)) TF (
    .en(1'b0), .C(CLK_t), .dir(1'b0), .in({1'b1, BUS[2:0]}), .ld(~nLD_TF), .clr(~nR),
    .out({nCOPY, TF_2, TF_1, TF_0}));  // open: ovf
  assign BUS = ~nOE_MEM ? RAM_q : 8'bz;  // DriverInvSel driverinvsel_3
  // Probe on {nCOPY, TF_2, TF_1, TF_0}
  // Probe on ADDRESS
  // NAnd nand_5 has open pins: In_1=1'b0, In_2=1'b0, out=open
  ROM #(.AddrBits(17), .Bits(8)) SIGNALS0 (
    .A({END_OF_COPY, nCOPY, TF_2, TF_1, TF_0, S, I}), .sel(1'b1),
    .D({LD_MEM, LD_T, nLD_TF, nLD_RH, nLD_RL, nLD_C, nLD_S, nLD_I}));
  ROM #(.AddrBits(17), .Bits(8)) SIGNALS1 (
    .A({END_OF_COPY, nCOPY, TF_2, TF_1, TF_0, S, I}), .sel(1'b1),
    .D({SEL_nM_CN, SEL_C2, SEL_C1, SEL_C0, nOE_ALU, nOE_MEM, nOE_T, INC_R}));
  nand nand_6 (nOE_GPI, nLD_C, SEL_C0);
  nand nand_7 (nLD_GPO, nLD_C, SEL_C1);
  ROM #(.AddrBits(19), .Bits(8)) ALU (
    .A({C2, C1, C0, R_8__15, R_8__11, R_0__7, END_OF_COPY, R_0__3}), .sel(1'b1), .D(ALU_d));
  // NAnd nand_8 has open pins: In_1=1'b0, In_2=1'b0, out=open
  assign BUS = ~nOE_ALU ? ALU_d : 8'bz;  // DriverInvSel driverinvsel_4
  // Probe on ALU_d

  // Other names for the same wires on the sheet: BUS_0 = BUS[0]; BUS_0__3[3:0] = BUS[3:0]; BUS_1 = BUS[1];
  //   BUS_2 = BUS[2]; BUS_4__7[3:0] = BUS[7:4]; BUS_7 = BUS[7]; R_0__7[4:0] = {END_OF_COPY, R_0__3};
  //   R_3__7[3:0] = {R_0__7, END_OF_COPY}; R_8__15[3:0] = R_8__11; R_12__15[3:0] = R_8__15

  // Notes on the sheet:
  //   clk: Hz: 16000
  //   Could be low/high 4-bit of
  //   the bus instead of SEL C
  //   Either low/high 4-bits
  //   0 could be C or SEL C
  //   This could be SEL C, C
  //   Could this come from a 
  //   latched bit, so we can toggle
  //   between two pages of 7 bits
  //   SIGNALS0 loads rom_signals0.bin
  //   SIGNALS1 loads rom_signals1.bin
  //   ALU loads rom_alu.bin
endmodule
