// Digital circuit a-cpu-sim-uart.dig as structural Verilog
// Simulates hardware UART
module a_cpu_sim_uart (
  input  CLK,
  input  nEN,
  input  nRTS,
  input  TX,
  output RX
);

  wire and_1_out, BYTE_SAMPLED, CLK_TELNET, comparator_1_eq, comparator_1_lt, comparator_3_gt, not_1_out,
       or_1_out, or_3_out, or_4_out, or_5_out, RX_AV, RX_BYTE_SAMPLED, RX_LAST_BIT, RX_NEXT_BIT, SAMPLE_BIT,
       TX_LAST_BIT;
  wire [3:0] counter_2_out, counter_3_out, counter_4_out, counter_5_out;
  wire [7:0] barrelshifter_1_out, counter_1_out, register_1_q;
  wire [8:0] not_2_out;
  wire [8:1] barrelshifter_2_out;

  Register #(.Bits(8)) register_1 (.D({TX, barrelshifter_1_out[6:0]}), .C(CLK), .en(SAMPLE_BIT), .Q(register_1_q));
  Counter #(.Bits(8)) counter_1 (
    .en(comparator_1_lt), .C(CLK), .clr(RX_BYTE_SAMPLED), .out(counter_1_out));  // open: ovf
  // Probe on register_1_q
  // Probe on register_1_q
  or or_1 (or_1_out, BYTE_SAMPLED, SAMPLE_BIT);
  BarrelShifter #(.Bits(8), .direction("right")) barrelshifter_1 (
    .in(register_1_q), .shift(4'b0001), .out(barrelshifter_1_out));
  // Probe on counter_1_out
  Comparator #(.Bits(8)) comparator_1 (
    .a(counter_1_out), .b(8'h1), .eq(comparator_1_eq), .lt(comparator_1_lt));  // open: gt
  Counter #(.Bits(4)) counter_2 (.en(1'b1), .C(CLK), .clr(or_1_out), .out(counter_2_out));  // open: ovf
  or or_2 (CLK_TELNET, TX_LAST_BIT, RX_LAST_BIT);
  // Probe on counter_2_out
  Comparator #(.Bits(4)) comparator_2 (.a(counter_2_out), .b(4'b1010), .eq(SAMPLE_BIT));  // open: gt, lt
  Telnet #(.telnetEscape("false"), .port(2323)) telnet_1 (
    .in(register_1_q), .C(CLK_TELNET), .wr(TX_LAST_BIT), .rd(not_1_out), .out(not_2_out[8:1]), .av(RX_AV));
  not not_1 (not_1_out, TX_LAST_BIT);
  or or_3 (or_3_out, RX_BYTE_SAMPLED, RX_NEXT_BIT);
  Counter #(.Bits(4)) counter_3 (.en(SAMPLE_BIT), .C(CLK), .clr(BYTE_SAMPLED), .out(counter_3_out));  // open: ovf
  Counter #(.Bits(4)) counter_4 (.en(comparator_1_eq), .C(CLK), .clr(or_3_out), .out(counter_4_out));  // open: ovf
  // Probe on counter_3_out
  // Probe on not_2_out[8:1]
  // Probe on not_2_out[8:1]
  or or_4 (or_4_out, TX, ~nEN);  // Or
  Comparator #(.Bits(4)) comparator_3 (
    .a(counter_3_out), .b(4'b1000), .gt(comparator_3_gt), .eq(TX_LAST_BIT));  // open: lt
  // Probe on counter_5_out
  // Probe on counter_4_out
  Comparator #(.Bits(4)) comparator_4 (.a(counter_4_out), .b(4'b1010), .eq(RX_NEXT_BIT));  // open: gt, lt
  not not_2 (not_2_out[0], RX_AV);
  BarrelShifter #(.Bits(9), .direction("right")) barrelshifter_2 (
    .in(not_2_out), .shift(counter_5_out), .out({barrelshifter_2_out, RX}));
  RS_FF rs_ff_1 (.S(~or_4_out), .C(CLK), .R(comparator_3_gt), .nQ(BYTE_SAMPLED));  // open: Q
  Counter #(.Bits(4)) counter_5 (.en(RX_NEXT_BIT), .C(CLK), .clr(RX_BYTE_SAMPLED), .out(counter_5_out));  // open: ovf
  // Probe on {barrelshifter_2_out, RX}
  Comparator #(.Bits(4)) comparator_5 (.a(counter_5_out), .b(4'b1001), .eq(RX_LAST_BIT));  // open: gt, lt
  // Probe on RX
  and and_1 (and_1_out, RX_BYTE_SAMPLED, nRTS);
  or or_5 (or_5_out, ~RX_AV, ~nEN, and_1_out);  // Or
  RS_FF rs_ff_2 (.S(~or_5_out), .C(CLK), .R(RX_LAST_BIT), .nQ(RX_BYTE_SAMPLED));  // open: Q

  // Other names for the same wires on the sheet: nCOPY = nEN
endmodule
