// Digital circuit custom-cpu.dig as structural Verilog
module custom_cpu (
  input  CLK
);

  wire and_1_out, and_2_out, BUTTON_nR, C0, C1, C2, CF, CLK_0, CLK_1, CLK_PULSE, CLK_T, comparator_1_eq,
       delay_1_out, delay_2_out, INC_M, LD_T, MHL_ovf, MLH_ovf, MLL_ovf, nINITF, nLD_C, nLD_F, nLD_IO,
       nLD_MEM, nLD_MH, nLD_ML, nLD_O, nLD_P0, nLD_P1, nLD_P2, nLD_P3, nLD_S, nM_C, nOE_ALU, nOE_C, nOE_MEM,
       nOE_P0, nOE_P1, nOE_P2, nOE_P3, nOE_T, not_1_out, not_2_out, nR, OE_IO, or_1_out, or_2_out, or_10_out,
       RX_AV, SEL_C0, SEL_C1, SEL_C2, SEL_nM_C, SF, SOFT_nR, ZF;
  wire [3:0] S;
  wire [7:0] ALU_d, BUS, GPIO_IN_q, GPIO_OUT_q, MH, ML, O, RAM_q, T_q;
  wire [7:7] dipswitch_1_out;
  wire [15:0] ADDRESS;

  Comparator #(.Bits(4)) comparator_1 (.a(S), .b(4'b0001), .eq(comparator_1_eq));  // open: gt, lt
  Break break_1 (.brk(nINITF));
  Break break_2 (.brk(CF));
  and and_1 (and_1_out, comparator_1_eq, nINITF);
  and and_2 (and_2_out, ~nLD_F, BUS[3]);  // And
  ROM #(.AddrBits(17), .Bits(8)) CONTROL0 (
    .A({1'b0, nINITF, SF, CF, ZF, S, O}), .sel(1'b1),
    .D({nLD_MEM, LD_T, OE_IO, nOE_T, nOE_MEM, INC_M, nLD_ML, nLD_MH}));
  ROM #(.AddrBits(17), .Bits(8)) CONTROL1 (
    .A({1'b1, nINITF, SF, CF, ZF, S, O}), .sel(1'b1),
    .D({SEL_nM_C, SEL_C2, SEL_C1, SEL_C0, nLD_C, nOE_ALU, nOE_C, nLD_F}));
  Break break_3 (.brk(and_1_out));
  Break break_4 (.brk(and_2_out));
  nand nand_1 (nLD_O, nLD_C, SEL_C0);
  nand nand_2 (nLD_S, nLD_C, SEL_C1);
  nand nand_3 (nLD_IO, nLD_C, SEL_C2);
  // Probe on BUS
  // Probe on ADDRESS
  or or_1 (or_1_out, CLK_PULSE, nLD_MEM);
  // Probe CLK MEM on or_1_out
  RAMAsync #(.AddrBits(16), .Bits(8)) RAM (.A(ADDRESS), .D(BUS), .we(~or_1_out), .Q(RAM_q));
  ROM #(.AddrBits(19), .Bits(8)) ALU (.A({C2, C1, C0, MH, ML}), .sel(1'b1), .D(ALU_d));
  assign BUS = ~nOE_MEM ? RAM_q : 8'bz;  // DriverInvSel driverinvsel_1
  // Probe on RAM_q
  assign BUS = ~nOE_ALU ? ALU_d : 8'bz;  // DriverInvSel driverinvsel_2
  // Probe on ALU_d
  Register #(.Bits(8)) u_O (.D(BUS), .C(CLK_1), .en(~nLD_O), .Q(O));
  Register #(.Bits(8)) T (.D(BUS), .C(CLK_T), .en(1'b1), .Q(T_q));
  CounterPreset #(.Bits(4)) MLL (
    .en(INC_M), .C(CLK_1), .dir(1'b0), .in(BUS[3:0]), .ld(~nLD_ML), .clr(~SOFT_nR), .out(ML[3:0]),
    .ovf(MLL_ovf));
  CounterPreset #(.Bits(4)) MLH (
    .en(MLL_ovf), .C(CLK_1), .dir(1'b0), .in(BUS[7:4]), .ld(~nLD_ML), .clr(~SOFT_nR), .out(ML[7:4]),
    .ovf(MLH_ovf));
  CounterPreset #(.Bits(4)) MHL (
    .en(MLH_ovf), .C(CLK_1), .dir(1'b0), .in(BUS[3:0]), .ld(~nLD_MH), .clr(~SOFT_nR), .out(MH[3:0]),
    .ovf(MHL_ovf));
  CounterPreset #(.Bits(4)) MHH (
    .en(MHL_ovf), .C(CLK_1), .dir(1'b0), .in(BUS[7:4]), .ld(~nLD_MH), .clr(~SOFT_nR), .out(MH[7:4]));  // open: ovf
  Register #(.Bits(4)) C (.D({SEL_nM_C, SEL_C2, SEL_C1, SEL_C0}), .C(CLK_1), .en(~nLD_C), .Q({nM_C, C2, C1, C0}));
  Register #(.Bits(4)) F (.D(BUS[3:0]), .C(CLK_1), .en(~nLD_F), .Q({nINITF, SF, CF, ZF}));
  CounterPreset #(.Bits(4)) u_S (
    .en(1'b1), .C(CLK_1), .dir(1'b0), .in(4'b0000), .ld(~nLD_S), .clr(~nR), .out(S));  // open: ovf
  // Probe on O
  assign BUS = ~nOE_T ? T_q : 8'bz;  // DriverInvSel driverinvsel_3
  // Probe on T_q
  // Probe on {nM_C, C2, C1, C0}
  // Probe on S
  // Probe on ML
  // Probe on MH
  assign BUS = ~nOE_C ? {{6{C2}}, C1, C0} : 8'bz;  // DriverInvSel driverinvsel_4
  Reset reset_1 (.out(nR));
  or or_2 (or_2_out, CLK, 1'b0);
  nand nand_4 (CLK_0, 1'b1, or_2_out);
  Multiplexer #(.Bits(4)) multiplexer_1 (.sel(nM_C), .in_0(ML[3:0]), .in_1({1'b0, C2, C1, C0}), .out(ADDRESS[3:0]));
  assign ADDRESS[7:4] = ML[7:4] | {4{nM_C}};  // Or or_3, 4 bits wide
  assign ADDRESS[11:8] = MH[3:0] | {4{nM_C}};  // Or or_4, 4 bits wide
  assign ADDRESS[15:12] = MH[7:4] | {4{nM_C}};  // Or or_5, 4 bits wide
  nand nand_5 (nOE_P0, OE_IO, C0);
  nand nand_6 (nOE_P1, OE_IO, C1);
  nand nand_7 (nOE_P2, OE_IO, C2);
  nand nand_8 (nOE_P3, OE_IO, nM_C);
  or or_6 (nLD_P0, nLD_IO, C0);
  or or_7 (nLD_P1, nLD_IO, C1);
  or or_8 (nLD_P2, nLD_IO, C2);
  or or_9 (nLD_P3, nLD_IO, nM_C);
  or or_10 (or_10_out, 1'b0, CLK_0);
  // Probe MBUS on ADDRESS[3:0]
  nand nand_9 (CLK_T, LD_T, CLK_0);
  nand nand_10 (CLK_PULSE, CLK, or_10_out);
  nand nand_11 (CLK_1, CLK_0, 1'b1);
  // Probe CLK T on CLK_T
  // Probe CLK P on CLK_PULSE
  // Probe CLK 1 on CLK_1
  or or_11 (SOFT_nR, BUTTON_nR, nLD_O);
  Button #(.activeLow("true")) RESET_2 (.out(BUTTON_nR));
  DipSwitch dipswitch_1 (.out(dipswitch_1_out[7]));
  Register #(.Bits(8)) GPIO_IN (.D({dipswitch_1_out[7], {7{1'b0}}}), .C(CLK_1), .en(~1'b0), .Q(GPIO_IN_q));
  Register #(.Bits(8)) GPIO_OUT (.D(BUS), .C(CLK_1), .en(~nLD_P3), .Q(GPIO_OUT_q));
  assign BUS = ~nOE_P3 ? GPIO_IN_q : 8'bz;  // DriverInvSel driverinvsel_5
  LED led_1 (.in(GPIO_OUT_q[0]));
  LED led_2 (.in(GPIO_OUT_q[1]));
  LED led_3 (.in(GPIO_OUT_q[2]));
  LED led_4 (.in(GPIO_OUT_q[3]));
  LED led_5 (.in(GPIO_OUT_q[4]));
  LED led_6 (.in(GPIO_OUT_q[5]));
  LED led_7 (.in(GPIO_OUT_q[6]));
  LED led_8 (.in(GPIO_OUT_q[7]));
  Delay delay_1 (.in(nLD_P0), .out(delay_1_out));
  Delay delay_2 (.in(nOE_P0), .out(delay_2_out));
  not not_1 (not_1_out, delay_1_out);
  not not_2 (not_2_out, delay_2_out);
  Telnet #(.telnetEscape("false"), .port(2323)) IO_UART (
    .in(BUS), .C(CLK_1), .wr(not_1_out), .rd(not_2_out), .out(BUS), .av(RX_AV));

  // Other names for the same wires on the sheet: nM_C_4bit[3:0] = {4{nM_C}}; BUS_L[3:0] = BUS[3:0];
  //   BUS_H[3:0] = BUS[7:4]; MHH[3:0] = MH[7:4]; MHL[3:0] = MH[3:0]; MLH[3:0] = ML[7:4]; MLL[3:0] = ML[3:0]

  // Notes on the sheet:
  //   CLK: Hz: 2000
  //   contents of CONTROL0 (hex, n*v repeats v):
  //   4*10,4*f2,1,5,1,5,248*10,4*f2,4*10,244*20,4*10,4*f2,4*20,244*30
  //   ,4*10,4*f2,4*30,244*40,4*10,4*f2,4*40,244*50,4*10,4*f2,4*50,244*60
  //   ,4*10,4*f2,4*60,244*70,4*10,4*f2,4*70,244*88,4*10,4*f2,4*80,244*98
  //   ,4*10,4*f2,4*90,244*a8,4*10,4*f2,4*a0,244*b8,4*10,4*f2,4*b0,244*c8
  //   ,4*10,4*f2,4*c0,244*d8,4*10,4*f2,4*d0,244*e8,4*10,4*f2,4*e0,244*f8
  //   ,4*10,4*f2,4*f0,244*7,4*10,4*f2,1,5,1,5,248*10,4*f2,4*10,244*20
  //   ,4*10,4*f2,4*20,244*30,4*10,4*f2,4*30,244*40,4*10,4*f2,4*40,244*50
  //   ,4*10,4*f2,4*50,244*60,4*10,4*f2,4*60,244*70,4*10,4*f2,4*70,244*88
  //   ,4*10,4*f2,4*80,244*98,4*10,4*f2,4*90,244*a8,4*10,4*f2,4*a0,244*b8
  //   ,4*10,4*f2,4*b0,244*c8,4*10,4*f2,4*c0,244*d8,4*10,4*f2,4*d0,244*e8
  //   ,4*10,4*f2,4*e0,244*f8,4*10,4*f2,4*f0,244*7,4*20,1,5,1,5,4*10
  //   ,248*20,1,5,1,5,4*20,244*30,4*20,1,5,1,5,4*30,244*40,4*20,1,5
  //   ,1,5,4*40,244*50,4*20,1,5,1,5,4*50,244*60,4*20,1,5,1,5,4*60,244*70
  //   ,4*20,1,5,1,5,4*70,244*88,4*20,1,5,1,5,4*80,244*98,4*20,1,5,1
  //   ,5,4*90,244*a8,4*20,1,5,1,5,4*a0,244*b8,4*20,1,5,1,5,4*b0,244*c8
  //   ,4*20,1,5,1,5,4*c0,244*d8,4*20,1,5,1,5,4*d0,244*e8,4*20,1,5,1
  //   ,5,4*e0,244*f8,4*20,1,5,1,5,4*f0,244*7,4*20,1,5,1,5,3,7,3,7,244*16
  //   ,4*20,1,5,1,5,4*10,248*20,1,5,1,5,4*20,244*30,4*20,1,5,1,5,4*30
  //   ,244*40,4*20,1,5,1,5,4*40,244*50,4*20,1,5,1,5,4*50,244*60,4*20
  //   ,1,5,1,5,4*60,244*70,4*20,1,5,1,5,4*70,244*88,4*20,1,5,1,5,4*80
  //   ,244*98,4*20,1,5,1,5,4*90,244*a8,4*20,1,5,1,5,4*a0,244*b8,4*20
  //   ,1,5,1,5,4*b0,244*c8,4*20,1,5,1,5,4*c0,244*d8,4*20,1,5,1,5,4*d0
  //   ,244*e8,4*20,1,5,1,5,4*e0,244*f8,4*20,1,5,1,5,4*f0,244*7,4*20
  //   ,1,5,1,5,3,7,3,7,244*16,4*30,4*10,4*20,248*30,4*10,4*30,244*40
  //   ,4*30,4*10,4*40,244*50,4*30,4*10,4*50,244*60,4*30,4*10,4*60,244*70
  //   ,4*30,4*10,4*70,244*88,4*30,4*10,4*80,244*98,4*30,4*10,4*90,244*a8
  //   ,4*30,4*10,4*a0,244*b8,4*30,4*10,4*b0,244*c8,4*30,4*10,4*c0,244*d8
  //   ,4*30,4*10,4*d0,244*e8,4*30,4*10,4*e0,244*f8,4*30,4*10,4*f0,244*7
  //   ,4*30,4*10,3,7,3,7,244*16,4*30,4*10,4*12,244*26,4*30,4*10,4*20
  //   ,248*30,4*10,4*30,244*40,4*30,4*10,4*40,244*50,4*30,4*10,4*50
  //   ,244*60,4*30,4*10,4*60,244*70,4*30,4*10,4*70,244*88,4*30,4*10
  //   ,4*80,244*98,4*30,4*10,4*90,244*a8,4*30,4*10,4*a0,244*b8,4*30
  //   ,4*10,4*b0,244*c8,4*30,4*10,4*c0,244*d8,4*30,4*10,4*d0,244*e8
  //   ,4*30,4*10,4*e0,244*f8,4*30,4*10,4*f0,244*7,4*30,4*10,3,7,3,7
  //   ,244*16,4*30,4*10,4*12,244*26,4*40,4*20,4*30,248*40,4*20,4*40
  //   ,244*50,4*40,4*20,4*50,244*60,4*40,4*20,4*60,244*70,4*40,4*20
  //   ,4*70,244*88,4*40,4*20,4*80,244*98,4*40,4*20,4*90,244*a8,4*40
  //   ,4*20,4*a0,244*b8,4*40,4*20,4*b0,244*c8,4*40,4*20,4*c0,244*d8
  //   ,4*40,4*20,4*d0,244*e8,4*40,4*20,4*e0,244*f8,4*40,4*20,4*f0,244*7
  //   ,4*40,4*20,3,7,3,7,244*16,4*40,4*20,4*12,244*26,4*40,4*20,4*22
  //   ,244*36,4*40,4*20,4*30,248*40,4*20,4*40,244*50,4*40,4*20,4*50
  //   ,244*60,4*40,4*20,4*60,244*70,4*40,4*20,4*70,244*88,4*40,4*20
  //   ,4*80,244*98,4*40,4*20,4*90,244*a8,4*40,4*20,4*a0,244*b8,4*40
  //   ,4*20,4*b0,244*c8,4*40,4*20,4*c0,244*d8,4*40,4*20,4*d0,244*e8
  //   ,4*40,4*20,4*e0,244*f8,4*40,4*20,4*f0,244*7,4*40,4*20,3,7,3,7
  //   ,244*16,4*40,4*20,4*12,244*26,4*40,4*20,4*22,244*36,4*50,4*30
  //   ,4*40,248*50,4*30,4*50,244*60,4*50,4*30,4*60,244*70,4*50,4*30
  //   ,4*70,244*88,4*50,4*30,4*80,244*98,4*50,4*30,4*90,244*a8,4*50
  //   ,4*30,4*a0,244*b8,4*50,4*30,4*b0,244*c8,4*50,4*30,4*c0,244*d8
  //   ,4*50,4*30,4*d0,244*e8,4*50,4*30,4*e0,244*f8,4*50,4*30,4*f0,244*7
  //   ,4*50,4*30,3,7,3,7,244*16,4*50,4*30,4*12,244*26,4*50,4*30,4*22
  //   ,244*36,4*50,4*30,4*32,244*46,4*50,4*30,4*40,248*50,4*30,4*50
  //   ,244*60,4*50,4*30,4*60,244*70,4*50,4*30,4*70,244*88,4*50,4*30
  //   ,4*80,244*98,4*50,4*30,4*90,244*a8,4*50,4*30,4*a0,244*b8,4*50
  //   ,4*30,4*b0,244*c8,4*50,4*30,4*c0,244*d8,4*50,4*30,4*d0,244*e8
  //   ,4*50,4*30,4*e0,244*f8,4*50,4*30,4*f0,244*7,4*50,4*30,3,7,3,7
  //   ,244*16,4*50,4*30,4*12,244*26,4*50,4*30,4*22,244*36,4*50,4*30
  //   ,4*32,244*46,4*60,4*40,4*50,248*60,4*40,4*60,244*70,4*60,4*40
  //   ,4*70,244*88,4*60,4*40,4*80,244*98,4*60,4*40,4*90,244*a8,4*60
  //   ,4*40,4*a0,244*b8,4*60,4*40,4*b0,244*c8,4*60,4*40,4*c0,244*d8
  //   ,4*60,4*40,4*d0,244*e8,4*60,4*40,4*e0,244*f8,4*60,4*40,4*f0,244*7
  //   ,4*60,4*40,3,7,3,7,244*16,4*60,4*40,4*12,244*26,4*60,4*40,4*22
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  //   contents of CONTROL1 (hex, n*v repeats v):
  //   4*10,4*f2,1,5,1,5,248*10,4*f2,4*10,244*20,4*10,4*f2,4*20,244*30
  //   ,4*10,4*f2,4*30,244*40,4*10,4*f2,4*40,244*50,4*10,4*f2,4*50,244*60
  //   ,4*10,4*f2,4*60,244*70,4*10,4*f2,4*70,244*88,4*10,4*f2,4*80,244*98
  //   ,4*10,4*f2,4*90,244*a8,4*10,4*f2,4*a0,244*b8,4*10,4*f2,4*b0,244*c8
  //   ,4*10,4*f2,4*c0,244*d8,4*10,4*f2,4*d0,244*e8,4*10,4*f2,4*e0,244*f8
  //   ,4*10,4*f2,4*f0,244*7,4*10,4*f2,1,5,1,5,248*10,4*f2,4*10,244*20
  //   ,4*10,4*f2,4*20,244*30,4*10,4*f2,4*30,244*40,4*10,4*f2,4*40,244*50
  //   ,4*10,4*f2,4*50,244*60,4*10,4*f2,4*60,244*70,4*10,4*f2,4*70,244*88
  //   ,4*10,4*f2,4*80,244*98,4*10,4*f2,4*90,244*a8,4*10,4*f2,4*a0,244*b8
  //   ,4*10,4*f2,4*b0,244*c8,4*10,4*f2,4*c0,244*d8,4*10,4*f2,4*d0,244*e8
  //   ,4*10,4*f2,4*e0,244*f8,4*10,4*f2,4*f0,244*7,4*20,1,5,1,5,4*10
  //   ,248*20,1,5,1,5,4*20,244*30,4*20,1,5,1,5,4*30,244*40,4*20,1,5
  //   ,1,5,4*40,244*50,4*20,1,5,1,5,4*50,244*60,4*20,1,5,1,5,4*60,244*70
  //   ,4*20,1,5,1,5,4*70,244*88,4*20,1,5,1,5,4*80,244*98,4*20,1,5,1
  //   ,5,4*90,244*a8,4*20,1,5,1,5,4*a0,244*b8,4*20,1,5,1,5,4*b0,244*c8
  //   ,4*20,1,5,1,5,4*c0,244*d8,4*20,1,5,1,5,4*d0,244*e8,4*20,1,5,1
  //   ,5,4*e0,244*f8,4*20,1,5,1,5,4*f0,244*7,4*20,1,5,1,5,3,7,3,7,244*16
  //   ,4*20,1,5,1,5,4*10,248*20,1,5,1,5,4*20,244*30,4*20,1,5,1,5,4*30
  //   ,244*40,4*20,1,5,1,5,4*40,244*50,4*20,1,5,1,5,4*50,244*60,4*20
  //   ,1,5,1,5,4*60,244*70,4*20,1,5,1,5,4*70,244*88,4*20,1,5,1,5,4*80
  //   ,244*98,4*20,1,5,1,5,4*90,244*a8,4*20,1,5,1,5,4*a0,244*b8,4*20
  //   ,1,5,1,5,4*b0,244*c8,4*20,1,5,1,5,4*c0,244*d8,4*20,1,5,1,5,4*d0
  //   ,244*e8,4*20,1,5,1,5,4*e0,244*f8,4*20,1,5,1,5,4*f0,244*7,4*20
  //   ,1,5,1,5,3,7,3,7,244*16,4*30,4*10,4*20,248*30,4*10,4*30,244*40
  //   ,4*30,4*10,4*40,244*50,4*30,4*10,4*50,244*60,4*30,4*10,4*60,244*70
  //   ,4*30,4*10,4*70,244*88,4*30,4*10,4*80,244*98,4*30,4*10,4*90,244*a8
  //   ,4*30,4*10,4*a0,244*b8,4*30,4*10,4*b0,244*c8,4*30,4*10,4*c0,244*d8
  //   ,4*30,4*10,4*d0,244*e8,4*30,4*10,4*e0,244*f8,4*30,4*10,4*f0,244*7
  //   ,4*30,4*10,3,7,3,7,244*16,4*30,4*10,4*12,244*26,4*30,4*10,4*20
  //   ,248*30,4*10,4*30,244*40,4*30,4*10,4*40,244*50,4*30,4*10,4*50
  //   ,244*60,4*30,4*10,4*60,244*70,4*30,4*10,4*70,244*88,4*30,4*10
  //   ,4*80,244*98,4*30,4*10,4*90,244*a8,4*30,4*10,4*a0,244*b8,4*30
  //   ,4*10,4*b0,244*c8,4*30,4*10,4*c0,244*d8,4*30,4*10,4*d0,244*e8
  //   ,4*30,4*10,4*e0,244*f8,4*30,4*10,4*f0,244*7,4*30,4*10,3,7,3,7
  //   ,244*16,4*30,4*10,4*12,244*26,4*40,4*20,4*30,248*40,4*20,4*40
  //   ,244*50,4*40,4*20,4*50,244*60,4*40,4*20,4*60,244*70,4*40,4*20
  //   ,4*70,244*88,4*40,4*20,4*80,244*98,4*40,4*20,4*90,244*a8,4*40
  //   ,4*20,4*a0,244*b8,4*40,4*20,4*b0,244*c8,4*40,4*20,4*c0,244*d8
  //   ,4*40,4*20,4*d0,244*e8,4*40,4*20,4*e0,244*f8,4*40,4*20,4*f0,244*7
  //   ,4*40,4*20,3,7,3,7,244*16,4*40,4*20,4*12,244*26,4*40,4*20,4*22
  //   ,244*36,4*40,4*20,4*30,248*40,4*20,4*40,244*50,4*40,4*20,4*50
  //   ,244*60,4*40,4*20,4*60,244*70,4*40,4*20,4*70,244*88,4*40,4*20
  //   ,4*80,244*98,4*40,4*20,4*90,244*a8,4*40,4*20,4*a0,244*b8,4*40
  //   ,4*20,4*b0,244*c8,4*40,4*20,4*c0,244*d8,4*40,4*20,4*d0,244*e8
  //   ,4*40,4*20,4*e0,244*f8,4*40,4*20,4*f0,244*7,4*40,4*20,3,7,3,7
  //   ,244*16,4*40,4*20,4*12,244*26,4*40,4*20,4*22,244*36,4*50,4*30
  //   ,4*40,248*50,4*30,4*50,244*60,4*50,4*30,4*60,244*70,4*50,4*30
  //   ,4*70,244*88,4*50,4*30,4*80,244*98,4*50,4*30,4*90,244*a8,4*50
  //   ,4*30,4*a0,244*b8,4*50,4*30,4*b0,244*c8,4*50,4*30,4*c0,244*d8
  //   ,4*50,4*30,4*d0,244*e8,4*50,4*30,4*e0,244*f8,4*50,4*30,4*f0,244*7
  //   ,4*50,4*30,3,7,3,7,244*16,4*50,4*30,4*12,244*26,4*50,4*30,4*22
  //   ,244*36,4*50,4*30,4*32,244*46,4*50,4*30,4*40,248*50,4*30,4*50
  //   ,244*60,4*50,4*30,4*60,244*70,4*50,4*30,4*70,244*88,4*50,4*30
  //   ,4*80,244*98,4*50,4*30,4*90,244*a8,4*50,4*30,4*a0,244*b8,4*50
  //   ,4*30,4*b0,244*c8,4*50,4*30,4*c0,244*d8,4*50,4*30,4*d0,244*e8
  //   ,4*50,4*30,4*e0,244*f8,4*50,4*30,4*f0,244*7,4*50,4*30,3,7,3,7
  //   ,244*16,4*50,4*30,4*12,244*26,4*50,4*30,4*22,244*36,4*50,4*30
  //   ,4*32,244*46,4*60,4*40,4*50,248*60,4*40,4*60,244*70,4*60,4*40
  //   ,4*70,244*88,4*60,4*40,4*80,244*98,4*60,4*40,4*90,244*a8,4*60
  //   ,4*40,4*a0,244*b8,4*60,4*40,4*b0,244*c8,4*60,4*40,4*c0,244*d8
  //   ,4*60,4*40,4*d0,244*e8,4*60,4*40,4*e0,244*f8,4*60,4*40,4*f0,244*7
  //   ,4*60,4*40,3,7,3,7,244*16,4*60,4*40,4*12,244*26,4*60,4*40,4*22
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  //   contents of ALU (hex, n*v repeats v):
  //   4*10,4*f2,1,5,1,5,248*10,4*f2,4*10,244*20,4*10,4*f2,4*20,244*30
  //   ,4*10,4*f2,4*30,244*40,4*10,4*f2,4*40,244*50,4*10,4*f2,4*50,244*60
  //   ,4*10,4*f2,4*60,244*70,4*10,4*f2,4*70,244*88,4*10,4*f2,4*80,244*98
  //   ,4*10,4*f2,4*90,244*a8,4*10,4*f2,4*a0,244*b8,4*10,4*f2,4*b0,244*c8
  //   ,4*10,4*f2,4*c0,244*d8,4*10,4*f2,4*d0,244*e8,4*10,4*f2,4*e0,244*f8
  //   ,4*10,4*f2,4*f0,244*7,4*10,4*f2,1,5,1,5,248*10,4*f2,4*10,244*20
  //   ,4*10,4*f2,4*20,244*30,4*10,4*f2,4*30,244*40,4*10,4*f2,4*40,244*50
  //   ,4*10,4*f2,4*50,244*60,4*10,4*f2,4*60,244*70,4*10,4*f2,4*70,244*88
  //   ,4*10,4*f2,4*80,244*98,4*10,4*f2,4*90,244*a8,4*10,4*f2,4*a0,244*b8
  //   ,4*10,4*f2,4*b0,244*c8,4*10,4*f2,4*c0,244*d8,4*10,4*f2,4*d0,244*e8
  //   ,4*10,4*f2,4*e0,244*f8,4*10,4*f2,4*f0,244*7,4*20,1,5,1,5,4*10
  //   ,248*20,1,5,1,5,4*20,244*30,4*20,1,5,1,5,4*30,244*40,4*20,1,5
  //   ,1,5,4*40,244*50,4*20,1,5,1,5,4*50,244*60,4*20,1,5,1,5,4*60,244*70
  //   ,4*20,1,5,1,5,4*70,244*88,4*20,1,5,1,5,4*80,244*98,4*20,1,5,1
  //   ,5,4*90,244*a8,4*20,1,5,1,5,4*a0,244*b8,4*20,1,5,1,5,4*b0,244*c8
  //   ,4*20,1,5,1,5,4*c0,244*d8,4*20,1,5,1,5,4*d0,244*e8,4*20,1,5,1
  //   ,5,4*e0,244*f8,4*20,1,5,1,5,4*f0,244*7,4*20,1,5,1,5,3,7,3,7,244*16
  //   ,4*20,1,5,1,5,4*10,248*20,1,5,1,5,4*20,244*30,4*20,1,5,1,5,4*30
  //   ,244*40,4*20,1,5,1,5,4*40,244*50,4*20,1,5,1,5,4*50,244*60,4*20
  //   ,1,5,1,5,4*60,244*70,4*20,1,5,1,5,4*70,244*88,4*20,1,5,1,5,4*80
  //   ,244*98,4*20,1,5,1,5,4*90,244*a8,4*20,1,5,1,5,4*a0,244*b8,4*20
  //   ,1,5,1,5,4*b0,244*c8,4*20,1,5,1,5,4*c0,244*d8,4*20,1,5,1,5,4*d0
  //   ,244*e8,4*20,1,5,1,5,4*e0,244*f8,4*20,1,5,1,5,4*f0,244*7,4*20
  //   ,1,5,1,5,3,7,3,7,244*16,4*30,4*10,4*20,248*30,4*10,4*30,244*40
  //   ,4*30,4*10,4*40,244*50,4*30,4*10,4*50,244*60,4*30,4*10,4*60,244*70
  //   ,4*30,4*10,4*70,244*88,4*30,4*10,4*80,244*98,4*30,4*10,4*90,244*a8
  //   ,4*30,4*10,4*a0,244*b8,4*30,4*10,4*b0,244*c8,4*30,4*10,4*c0,244*d8
  //   ,4*30,4*10,4*d0,244*e8,4*30,4*10,4*e0,244*f8,4*30,4*10,4*f0,244*7
  //   ,4*30,4*10,3,7,3,7,244*16,4*30,4*10,4*12,244*26,4*30,4*10,4*20
  //   ,248*30,4*10,4*30,244*40,4*30,4*10,4*40,244*50,4*30,4*10,4*50
  //   ,244*60,4*30,4*10,4*60,244*70,4*30,4*10,4*70,244*88,4*30,4*10
  //   ,4*80,244*98,4*30,4*10,4*90,244*a8,4*30,4*10,4*a0,244*b8,4*30
  //   ,4*10,4*b0,244*c8,4*30,4*10,4*c0,244*d8,4*30,4*10,4*d0,244*e8
  //   ,4*30,4*10,4*e0,244*f8,4*30,4*10,4*f0,244*7,4*30,4*10,3,7,3,7
  //   ,244*16,4*30,4*10,4*12,244*26,4*40,4*20,4*30,248*40,4*20,4*40
  //   ,244*50,4*40,4*20,4*50,244*60,4*40,4*20,4*60,244*70,4*40,4*20
  //   ,4*70,244*88,4*40,4*20,4*80,244*98,4*40,4*20,4*90,244*a8,4*40
  //   ,4*20,4*a0,244*b8,4*40,4*20,4*b0,244*c8,4*40,4*20,4*c0,244*d8
  //   ,4*40,4*20,4*d0,244*e8,4*40,4*20,4*e0,244*f8,4*40,4*20,4*f0,244*7
  //   ,4*40,4*20,3,7,3,7,244*16,4*40,4*20,4*12,244*26,4*40,4*20,4*22
  //   ,244*36,4*40,4*20,4*30,248*40,4*20,4*40,244*50,4*40,4*20,4*50
  //   ,244*60,4*40,4*20,4*60,244*70,4*40,4*20,4*70,244*88,4*40,4*20
  //   ,4*80,244*98,4*40,4*20,4*90,244*a8,4*40,4*20,4*a0,244*b8,4*40
  //   ,4*20,4*b0,244*c8,4*40,4*20,4*c0,244*d8,4*40,4*20,4*d0,244*e8
  //   ,4*40,4*20,4*e0,244*f8,4*40,4*20,4*f0,244*7,4*40,4*20,3,7,3,7
  //   ,244*16,4*40,4*20,4*12,244*26,4*40,4*20,4*22,244*36,4*50,4*30
  //   ,4*40,248*50,4*30,4*50,244*60,4*50,4*30,4*60,244*70,4*50,4*30
  //   ,4*70,244*88,4*50,4*30,4*80,244*98,4*50,4*30,4*90,244*a8,4*50
  //   ,4*30,4*a0,244*b8,4*50,4*30,4*b0,244*c8,4*50,4*30,4*c0,244*d8
  //   ,4*50,4*30,4*d0,244*e8,4*50,4*30,4*e0,244*f8,4*50,4*30,4*f0,244*7
  //   ,4*50,4*30,3,7,3,7,244*16,4*50,4*30,4*12,244*26,4*50,4*30,4*22
  //   ,244*36,4*50,4*30,4*32,244*46,4*50,4*30,4*40,248*50,4*30,4*50
  //   ,244*60,4*50,4*30,4*60,244*70,4*50,4*30,4*70,244*88,4*50,4*30
  //   ,4*80,244*98,4*50,4*30,4*90,244*a8,4*50,4*30,4*a0,244*b8,4*50
  //   ,4*30,4*b0,244*c8,4*50,4*30,4*c0,244*d8,4*50,4*30,4*d0,244*e8
  //   ,4*50,4*30,4*e0,244*f8,4*50,4*30,4*f0,244*7,4*50,4*30,3,7,3,7
  //   ,244*16,4*50,4*30,4*12,244*26,4*50,4*30,4*22,244*36,4*50,4*30
  //   ,4*32,244*46,4*60,4*40,4*50,248*60,4*40,4*60,244*70,4*60,4*40
  //   ,4*70,244*88,4*60,4*40,4*80,244*98,4*60,4*40,4*90,244*a8,4*60
  //   ,4*40,4*a0,244*b8,4*60,4*40,4*b0,244*c8,4*60,4*40,4*c0,244*d8
  //   ,4*60,4*40,4*d0,244*e8,4*60,4*40,4*e0,244*f8,4*60,4*40,4*f0,244*7
  //   ,4*60,4*40,3,7,3,7,244*16,4*60,4*40,4*12,244*26,4*60,4*40,4*22
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endmodule
