// Digital circuit simulation.dig as structural Verilog
module simulation (
  input  clk,
  input  in_3,
  output out_2
);

  wire and_1_out, C0, C1, C2, C3_SCLK, CLK_t, CLK_T_t, comparator_1_eq, comparator_2_gt, comparator_2_lt,
       comparator_3_eq, INC_M, LD_MEM, LD_T, MHL_ovf, MLH_ovf, MLL_ovf, nand_8_out, nand_9_out, nand_10_out,
       nand_11_out, nCLK, nLD_C, nLD_GPO, nLD_I, nLD_MH, nLD_ML, nLD_S, nLD_TF, nM_C, nOE_ALU, nOE_GPI,
       nOE_MEM, nOE_T, nR, nSCS, nWE_PULSE, or_1_out, RX, SEL_C0, SEL_C1, SEL_C2, SEL_C3, SEL_nM_C, SEL_TF2,
       T0, T1, T2, T3_MOSI, TX, UART_av;
  wire [3:0] multiplexer_1_out, or_2_out, or_3_out, or_4_out, S;
  wire [7:0] ALU_d, BUS, GPI_q, I, RAM_q, T_q;
  wire [7:1] UART_out;
  wire [7:3] GPO_q;
  wire [7:5] C_q;
  wire [15:0] M;

  Comparator #(.Bits(4)) comparator_1 (.a(S), .b(4'b0001), .eq(comparator_1_eq));  // open: gt, lt
  Comparator #(.Bits(8)) comparator_2 (.a(I), .b({8{1'b0}}), .gt(comparator_2_gt), .lt(comparator_2_lt));  // open: eq
  Comparator comparator_3 (.a(M[13]), .b(1'b1), .eq(comparator_3_eq));  // open: gt, lt
  nand nand_1 (SEL_TF2, BUS[2], SEL_nM_C);
  or or_1 (or_1_out, comparator_2_gt, comparator_2_lt);
  Break #(.Cycles(3000000)) break_1 (.brk(comparator_3_eq));
  Register #(.Bits(8)) u_I (.D(BUS), .C(CLK_t), .en(~nLD_I), .Q(I));
  CounterPreset #(.Bits(4)) u_S (
    .en(1'b1), .C(CLK_t), .dir(1'b0), .in(4'b0000), .ld(~nLD_S), .clr(~nR), .out(S));  // open: ovf
  and and_1 (and_1_out, comparator_1_eq, or_1_out);
  // Probe I on I
  // Probe S on S
  Break #(.Cycles(3000000)) break_2 (.brk(and_1_out));
  Reset reset_1 (.out(nR));
  ROM #(.AddrBits(17), .Bits(8)) INSTRUCTION1 (
    .A({M[13], T3_MOSI, T2, T1, T0, S, I}), .sel(1'b1),
    .D({INC_M, nLD_S, LD_MEM, LD_T, nLD_MH, nLD_ML, nLD_C, nLD_I}));
  ROM #(.AddrBits(17), .Bits(8)) INSTRUCTION2 (
    .A({M[13], T3_MOSI, T2, T1, T0, S, I}), .sel(1'b1),
    .D({SEL_nM_C, SEL_C3, SEL_C2, SEL_C1, SEL_C0, nOE_T, nOE_ALU, nOE_MEM}));
  ROM #(.AddrBits(19), .Bits(8)) ALU (.A({C2, C1, C0, M}), .sel(1'b1), .D(ALU_d));
  // Probe BUS on BUS
  nand nand_2 (nOE_GPI, nLD_C, SEL_C1);
  nand nand_3 (nLD_GPO, nLD_C, SEL_C2);
  nand nand_4 (nLD_TF, nLD_C, SEL_C3);
  assign BUS = ~nOE_ALU ? ALU_d : 8'bz;  // DriverInvSel driverinvsel_1
  nand nand_5 (nCLK, clk, 1'b1);
  nand nand_6 (CLK_t, nCLK, 1'b1);
  // Probe ~CLK on nCLK
  nand nand_7 (CLK_T_t, nCLK, LD_T);
  nand nand_8 (nand_8_out, nWE_PULSE, 1'b1);
  // Probe CLK on CLK_t
  nand nand_9 (nand_9_out, nand_8_out, 1'b1);
  Register #(.Bits(8)) T (.D(BUS), .C(CLK_T_t), .en(1'b1), .Q(T_q));
  Register #(.Bits(8)) C (
    .D({3'b000, SEL_nM_C, SEL_C3, SEL_C2, SEL_C1, SEL_C0}), .C(CLK_t), .en(~nLD_C),
    .Q({C_q, nM_C, C3_SCLK, C2, C1, C0}));
  CounterPreset #(.Bits(4)) TF (
    .en(1'b0), .C(CLK_t), .dir(1'b0), .in({BUS[7], SEL_TF2, BUS[1:0]}), .ld(~nLD_TF), .clr(~nR),
    .out({T3_MOSI, T2, T1, T0}));  // open: ovf
  CounterPreset #(.Bits(4)) MLL (
    .en(INC_M), .C(CLK_t), .dir(1'b0), .in(BUS[3:0]), .ld(~nLD_ML), .clr(~1'b1), .out(M[3:0]), .ovf(MLL_ovf));
  CounterPreset #(.Bits(4)) MLH (
    .en(MLL_ovf), .C(CLK_t), .dir(1'b0), .in(BUS[7:4]), .ld(~nLD_ML), .clr(~1'b1), .out(M[7:4]), .ovf(MLH_ovf));
  CounterPreset #(.Bits(4)) MHL (
    .en(MLH_ovf), .C(CLK_t), .dir(1'b0), .in(BUS[3:0]), .ld(~nLD_MH), .clr(~1'b1), .out(M[11:8]),
    .ovf(MHL_ovf));
  CounterPreset #(.Bits(4)) MHH (
    .en(MHL_ovf), .C(CLK_t), .dir(1'b0), .in(BUS[7:4]), .ld(~nLD_MH), .clr(~1'b1), .out(M[15:12]));  // open: ovf
  nand nand_10 (nand_10_out, nand_9_out, nWE_PULSE);
  // Probe T on T_q
  assign BUS = ~nOE_T ? T_q : 8'bz;  // DriverInvSel driverinvsel_2
  // Probe C on {C_q, nM_C, C3_SCLK, C2, C1, C0}
  // Probe MLL on M[3:0]
  nand nand_11 (nand_11_out, nand_10_out, 1'b1);
  nand nand_12 (nWE_PULSE, nCLK, LD_MEM);
  // Probe ~WE PULSE HW on nand_11_out
  // Probe ~WE PULSE on nWE_PULSE
  Multiplexer #(.Bits(4)) multiplexer_1 (
    .sel(nM_C), .in_0(M[3:0]), .in_1({C3_SCLK, C2, C1, C0}), .out(multiplexer_1_out));
  assign or_2_out = M[7:4] | {4{nM_C}};  // Or or_2, 4 bits wide
  assign or_3_out = M[11:8] | {4{nM_C}};  // Or or_3, 4 bits wide
  assign or_4_out = M[15:12] | {4{nM_C}};  // Or or_4, 4 bits wide
  // Probe M on M
  // Probe M on {or_4_out, or_3_out, or_2_out, multiplexer_1_out}
  RAMAsync #(.AddrBits(16), .Bits(8)) RAM (
    .A({or_4_out, or_3_out, or_2_out, multiplexer_1_out}), .D(BUS), .we(~nWE_PULSE), .Q(RAM_q));
  assign BUS = ~nOE_MEM ? RAM_q : 8'bz;  // DriverInvSel driverinvsel_3
  Register #(.Bits(8)) GPI (.D({T3_MOSI, {5{1'b0}}, in_3, RX}), .C(CLK_T_t), .en(1'b1), .Q(GPI_q));
  Register #(.Bits(8)) GPO (.D(BUS), .C(CLK_t), .en(~nLD_GPO), .Q({GPO_q, nSCS, out_2, TX}));
  assign BUS = ~nOE_GPI ? GPI_q : 8'bz;  // DriverInvSel driverinvsel_4
  // Probe on GPI_q
  LED led_1 (.in(GPO_q[3]));
  LED led_2 (.in(GPO_q[4]));
  LED led_3 (.in(GPO_q[5]));
  LED led_4 (.in(GPO_q[6]));
  LED led_5 (.in(GPO_q[7]));
  // Probe on I
  Telnet #(.telnetEscape("false"), .port(2323)) UART (
    .in({{6{1'b0}}, out_2, TX}), .C(CLK_t), .wr(1'b1), .rd(1'b1), .out({UART_out, RX}), .av(UART_av));
  // Probe on UART_av
  // Probe on {UART_out, RX}

  // Other names for the same wires on the sheet: nRTS = out_2; BUSL[3:0] = BUS[3:0]; BUSH[3:0] = BUS[7:4]; O0 = I[0];
  //   O1 = I[1]; O2 = I[2]; O3 = I[3]; O4 = I[4]; O5 = I[5]; O6 = I[6]; O7 = I[7]; MHH[3:0] = M[15:12];
  //   MHL[3:0] = M[11:8]; MISO = in_3; MLH[3:0] = M[7:4]; MLL[3:0] = M[3:0]

  // Notes on the sheet:
  //   clk: Hz: 16000
  //   in_3: default 1
  //   Need to assert SEL C to store actual BUS2 value (inverted), otherwise always 1
  //   Break after reset and I loaded
  //   Could LD S = LD O ? Special case at 0
  //   INSTRUCTION1 loads rom_instruction1.bin
  //   INSTRUCTION2 loads rom_instruction2.bin
  //   ALU loads rom_alu.bin
  //   This is probably not necessary
endmodule
